# Fritzing sketch fishpino (saved by Fritzing 0.9.3b)
stripboards: 5

parts:
  12V_POWER = Power plug
  RTC = DS1307 [package=so08]
  J1 = female pin header, 20 pins [form="♀ (female)"]  # not connected
  LCD_SCREEN = female pin header, 20 pins [form="♀ (female)"]
  Part1 = Arduino Mega 2560 (Rev3)
  Q2 = MOSFET-NCHANNEL [package=to220v]
  Q3 = MOSFET-NCHANNEL [package=to220v]
  Q5 = MOSFET-NCHANNEL [package=to220v]
  Q4 = MOSFET-NCHANNEL [package=to220v]
  R3 = Resistor [tolerance=±5% resistance=10k package=THT]
  R4 = Resistor [tolerance=±5% resistance=10k package=THT]
  R5 = Resistor [tolerance=±5% resistance=10k package=THT]
  U1 = ESP8266 WiFi Module [part_number=ESP8266]
  R6 = Resistor [tolerance=±5% resistance=1k package=THT]
  R7 = Resistor [tolerance=±5% resistance=1k package=THT]
  R8 = Resistor [tolerance=±5% resistance=1k package=THT]
  R9 = Resistor [tolerance=±5% resistance=10k package=THT]
  Composant2 = TFT 2.2 inch 320x240 w microSD [part_number=1480]
  RGB_Strip_LED1 = RGB Strip LED
  R2 = Resistor [tolerance=±5% resistance=10k package=THT]
  RGB_Strip_LED2 = RGB Strip LED
  F1 = Fan - Ventilador [package=THT]
  12V_POWER_2 = Power plug
  F2 = Fan - Ventilador [package=THT]
  F3 = Fan - Ventilador [package=THT]
  12V_POWER2 = Power plug
  J8 = Piezo Speaker
  S1 = PH meter [package=THT]
  R10 = Resistor [tolerance=±5% resistance=4.7k package=THT]
  DS1 = DS18B20 1-Wire Temperature Sensor [part_number=DS18B20]
  DS2 = DS18B20 1-Wire Temperature Sensor [part_number=DS18B20]
  DS3 = DS18B20 1-Wire Temperature Sensor [part_number=DS18B20]
  Composant3 = Lilypad Battery Connect
  IC1 = ULN2003A [package="DIP16 [THT]"]
  R11 = Resistor [tolerance=±5% resistance=56 package=THT]
  J9 = male pin header, 1 pin [form="♂ (male)"]
  J10 = male pin header, 1 pin [form="♂ (male)"]
  J11 = male pin header, 1 pin [form="♂ (male)"]
  J12 = male pin header, 1 pin [form="♂ (male)"]
  J13 = male pin header, 1 pin [form="♂ (male)"]
  J14 = male pin header, 1 pin [form="♂ (male)"]
  J15 = male pin header, 1 pin [form="♂ (male)"]
  J16 = male pin header, 1 pin [form="♂ (male)"]
  J17 = male pin header, 1 pin [form="♂ (male)"]
  J18 = male pin header, 1 pin [form="♂ (male)"]
  J19 = male pin header, 1 pin [form="♂ (male)"]
  J20 = male pin header, 1 pin [form="♂ (male)"]
  J21 = male pin header, 1 pin [form="♂ (male)"]
  J22 = male pin header, 1 pin [form="♂ (male)"]
  J23 = male pin header, 1 pin [form="♂ (male)"]
  J24 = male pin header, 1 pin [form="♂ (male)"]
  J25 = male pin header, 1 pin [form="♂ (male)"]
  J26 = male pin header, 1 pin [form="♂ (male)"]
  J27 = male pin header, 1 pin [form="♂ (male)"]
  J28 = male pin header, 1 pin [form="♂ (male)"]
  J29 = male pin header, 1 pin [form="♂ (male)"]
  J30 = male pin header, 1 pin [form="♂ (male)"]
  J31 = male pin header, 1 pin [form="♂ (male)"]
  J32 = male pin header, 1 pin [form="♂ (male)"]
  J33 = male pin header, 1 pin [form="♂ (male)"]
  J34 = male pin header, 1 pin [form="♂ (male)"]
  J35 = male pin header, 1 pin [form="♂ (male)"]
  J36 = male pin header, 1 pin [form="♂ (male)"]
  J37 = male pin header, 1 pin [form="♂ (male)"]
  J38 = male pin header, 1 pin [form="♂ (male)"]
  J39 = male pin header, 1 pin [form="♂ (male)"]
  J40 = male pin header, 1 pin [form="♂ (male)"]
  J41 = male pin header, 1 pin [form="♂ (male)"]
  J42 = male pin header, 1 pin [form="♂ (male)"]
  J43 = male pin header, 1 pin [form="♂ (male)"]
  J44 = male pin header, 1 pin [form="♂ (male)"]
  J45 = male pin header, 1 pin [form="♂ (male)"]
  J46 = male pin header, 1 pin [form="♂ (male)"]  # not connected
  J47 = male pin header, 1 pin [form="♂ (male)"]
  8_Channel_Relay1 = 8 Channel Power Relay
  R12 = Resistor [tolerance=±5% resistance=10k package=THT]
  U2 = 2-Channel 5v Relay Shield [package=relay-2ch5v10a]
  BRASSAGE_PWM_/8 = DC Motor
  BRASSAGE_PWM_/9 = DC Motor
  12V_POWER3 = Power plug
  J48 = male pin header, 1 pin [form="♂ (male)"]
  J49 = male pin header, 1 pin [form="♂ (male)"]
  J50 = male pin header, 1 pin [form="♂ (male)"]
  J51 = male pin header, 1 pin [form="♂ (male)"]
  J52 = male pin header, 1 pin [form="♂ (male)"]
  Q9 = TRANSISTOR_NPN [package=to-92-ammo]  # not connected
  R13 = Resistor [tolerance=±5% resistance=220 package=THT]
  J53 = male pin header, 1 pin [form="♂ (male)"]
  J54 = male pin header, 1 pin [form="♂ (male)"]
  J55 = male pin header, 1 pin [form="♂ (male)"]
  J56 = male pin header, 1 pin [form="♂ (male)"]

nets:
  GND: 12V_POWER.GND, RTC.GND, Part1.GND, U1.GPIO_2, U1.GND, 12V_POWER_2.GND, 12V_POWER2.GND, J8.pin1, S1.pin3, DS1.GND, DS2.GND, DS3.GND, IC1.0V, J15.pin1, J16.pin1, J18.pin1, J25.pin1, J26.pin1, J27.pin1, J28.pin1, J29.pin1, J31.pin1, J33.pin1, J37.pin1, J40.pin1, J42.pin1, J47.pin1, 8_Channel_Relay1.GND, R12.Pin_1, U2.GND, J48.pin1
  N1: 12V_POWER.VCC, RGB_Strip_LED1.Common_Connect#4, RGB_Strip_LED2.Common_Connect#4, J13.pin1, J14.pin1, J17.pin1
  N2: RTC.SDA, Part1.D20/SDA, Part1.SDA
  N3: RTC.SCL, Part1.D21/SCL, Part1.SCL
  VCC: RTC.VCC, Part1.5V, S1.pin2, R10.Pin_1, DS1.DQ, DS2.DQ, DS3.DQ, R11.Pin_1, J24.pin1, J30.pin1, J32.pin1, J35.pin1, J38.pin1, J41.pin1, J43.pin1, U2.VCC, J53.pin1, J54.pin1
  N4: LCD_SCREEN.pin2, R11.Pin_0
  N5: Part1.A8, Composant3.-
  N6: Part1.A9, 8_Channel_Relay1.IN3
  N7: Part1.A10, S1.pin1
  N8: Part1.A11, J8.pin2
  N9: Part1.A12, 8_Channel_Relay1.IN2
  N10: Part1.A14, 8_Channel_Relay1.IN1
  VDD: Part1.A15, R10.Pin_0, DS1.VDD, DS2.VDD, DS3.VDD, J34.pin1, J36.pin1, J39.pin1, J44.pin1, J45.pin1
  N11: Part1.A0, IC1.In_4
  N12: Part1.A1, IC1.In_5
  N13: Part1.A2, IC1.In_6
  N14: Part1.A3, IC1.In_7
  N15: Part1.A5, 8_Channel_Relay1.IN4
  N16: Part1.D19/RX1, U1.TXD
  N17: Part1.D18/TX1, R6.Pin_1, J23.pin1
  N18: Part1.D13_PWM, R13.Pin_1
  N19: Part1.D9_PWM, U2.IN1
  N20: Part1.D8_PWM, U2.IN2
  3V3: Part1.3V3, U1.VCC, R9.Pin_0, J21.pin1, J22.pin1
  N21: Part1.D2_PWM, Q5.G, R5.Pin_0, R5.Pin_1
  N22: Part1.D5_PWM, Q3.G, R3.Pin_0, R3.Pin_1
  N23: Part1.D6_PWM, Q2.G, R2.Pin_0, R2.Pin_1
  N24: Part1.D7_PWM, Q4.G, R4.Pin_0, R4.Pin_1
  N25: Part1.D38, Composant2.MOSI
  N26: Part1.D39, Composant2.MISO
  N27: Part1.D40, Composant2.SCLK
  N28: Part1.D41, Composant2.BACKLIGHT
  N29: Part1.D42, Composant2.VIN
  N30: Part1.D43, Composant2.DC
  N31: Part1.D44, IC1.In_1
  N32: Part1.D45, IC1.In_2
  N33: Part1.D46, IC1.In_3
  N34: Part1.D47, Composant2.RESET
  N35: Part1.D48, Composant2.SDCS
  N36: Part1.D49, Composant2.LCDCS
  N37: Q2.D, RGB_Strip_LED1.Red_Connect#6, J9.pin1
  N38: Q3.D, RGB_Strip_LED2.Green_Connect#7, J10.pin1
  N39: Q5.D, RGB_Strip_LED1.Green_Connect#7, J12.pin1
  N40: Q4.D, RGB_Strip_LED1.Blue_Connect#5, J11.pin1
  N41: U1.RXD, R6.Pin_0, R8.Pin_1, J19.pin1
  N42: U1.GPIO_16, U1.CH_PD, R9.Pin_1, J20.pin1
  N43: R7.Pin_0, J50.pin1, J51.pin1, J52.pin1, J55.pin1, J56.pin1
  N44: R7.Pin_1, R8.Pin_0
  5V: F1.5V, 12V_POWER_2.VCC, F2.5V, F3.5V, IC1.COM_-_Common
  VCC_2: 12V_POWER2.VCC, 8_Channel_Relay1.VCC
  N45: Composant3.+, R12.Pin_0, J49.pin1
  N46: IC1.Out_7, 8_Channel_Relay1.IN8
  N47: IC1.Out_6, 8_Channel_Relay1.IN7
  N48: IC1.Out_5, 8_Channel_Relay1.IN6
  N49: IC1.Out_4, 8_Channel_Relay1.IN5
  N50: U2.K1-In, U2.K2-In, 12V_POWER3.GND
  N51: U2.K1-On, BRASSAGE_PWM_/8.pin_2
  N52: U2.K2-On, BRASSAGE_PWM_/9.pin_2
  N53: BRASSAGE_PWM_/8.pin_1, BRASSAGE_PWM_/9.pin_1, 12V_POWER3.VCC

notes:
  POWER SUPPLY — 12V
  Light1
  Light2
  Filter
  Circ
  Heater
  CO2
  Aux 1
  Aux 2
  +12v
  GND
  LIGHT 1
  19 - LCD_BL
  20 - NOT USED
  21 - LCD_DB0
  22 - LCD_DB1
  23 - LCD_DB2
  24  - LCD_DB3
  25 - LCD_DB4
  26  - LCD_DB5
  27  - LCD_DB6
  28  - LCD_DB7
  29 - TouchP_CLK
  30 - TouchP_CS
  31 - TouchP_DIN
  32 - TouchP_BUSY
  33 - TouchP_OUT
  34 - TouchP_Penirq
  35 - SD_OUT
  36 - SD_SCK
  37 - SD_DIN
  38 - SD_CS
  39 - NOT USED
  40 - NOT USED
  3.2" TFT DISPLAY
  5- LCD_WR
  12 - LCD_DB13
  15 - LCD_CS
  6 - LCD_RD
  16 - NOT USED
  7 - LCD_DB8
  10 - LCD_DB11
  13 - LCD_DB14
  11 - LCD_DB12
  4 - LCD_RS
  14 - LCD_DB15
  2 - VCC
  9 - LCD_DB10
  3 - UNUSED
  18 - NOT USED
  1 - GND
  17 - LCD_RESET
  8 - LCD_DB9

custom parts:
  ESP8266 WiFi Module: Generic WiFi Module based on the ESP8266 with onboard PCB antenna and UART communications
  TFT 2.2 inch 320x240 w microSD: This lovely little display breakout is the best way to add a small, colorful and bright display to any project. Since the display uses 4-wire SPI to communicate and has its own pixel-addressable frame buffer, it can be used with every kind of microcontroller. Even a very small one with low memory and few pins available! The 2.2" display has 320x240 color pixels.
  RGB Strip LED: A tri-color Strip LED with red, green and blue. Pin order: red - common cathode - blue - green
  Fan - Ventilador: Ventilador de 2 pines, se encuentra comunmente en computadoras de escritorio
  8 Channel Power Relay: An 8 channel power relay. The module operates at 5V.
  2-Channel 5v Relay Shield: 2 Channel 5v Relay Shield w. 2x SPD-06VDC-SD-C
